# Fritzing sketch Raspi-Physical-Computing (saved by Fritzing 0.9.9b)
breadboards: 1

parts:
  Raspberry_Pi_2 = Raspberry Pi 4 [part_number=RPI-4-b]
  LED1 = LED - 5mm [color="Red (633nm)" current=0.030 package="5 mm [THT]"]
  R1 = Resistor [tolerance=±5% power=0.25 resistance=220 package=THT]
  LED2 = LED - 5mm [color="Yellow (595nm)" current=0.030 package="5 mm [THT]"]
  R2 = Resistor [tolerance=±5% power=0.25 resistance=220 package=THT]
  LED3 = LED - 5mm [color="Green (565nm)" current=0.030 package="5 mm [THT]"]
  R3 = Resistor [tolerance=±5% power=0.25 resistance=220 package=THT]
  S2 = Pushbutton [package="[THT]"]
  DHT23 = Humidity and Temperature Sensor RHT03
  R6 = Resistor [tolerance=±5% resistance=4.7k power=0.25 package=THT]
  BMP_280 = Adafruit_BMP280

nets:
  3V3: Raspberry_Pi_2.3v3, DHT23.Vcc, BMP_280.VIN
  N1: Raspberry_Pi_2.GPIO2, BMP_280.SDI/SDA
  N2: Raspberry_Pi_2.GPIO3, BMP_280.SCK/SCL
  N3: Raspberry_Pi_2.GPIO13, LED1.cathode
  N4: Raspberry_Pi_2.GPIO19, LED2.cathode
  N5: Raspberry_Pi_2.GPIO26, LED3.cathode
  N6: Raspberry_Pi_2.GPIO20, S2.Pin_1, S2.Pin_2
  N7: Raspberry_Pi_2.GPIO16, DHT23.Data-signal, R6.Pin_1
  GND: Raspberry_Pi_2.GND, R1.Pin_1, R2.Pin_1, R3.Pin_1, S2.Pin_3, S2.Pin_4, DHT23.GND_2, R6.Pin_0, BMP_280.GND
  N8: LED1.anode, R1.Pin_0
  N9: LED2.anode, R2.Pin_0
  N10: LED3.anode, R3.Pin_0

notes:
  3.3V
  GND
  GPIO 13
  GPIO 19
  GPIO 26
  GPIO 20
  GPIO 16
  GPIO3 SCL / SCK
  GPIO2 SDA / SDI

custom parts:
  Raspberry Pi 4: The RPi4, a faster version of the awesome Raspberry Pi 2 B ARM Board with 40 pin gpio. Ready for special Raspberry Pi B+ and RPi2 Hat (Hardware attached (on) top)
  Adafruit_BMP280: Bosch has stepped up their game with their new BMP280 sensor, an environmental sensor with temperature, barometric pressure that is the next generation upgrade to the BMP085/BMP180/BMP183. This sensor is great for all sorts of weather sensing and can even be used in both I2C and SPI! This precision sensor from Bosch is the best low-cost, precision sensing solution for measuring barometric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
